// Logisim project lab4.circ as structural Verilog: 13 circuits, main circuit main
module main (
  input  A,
  input  B,
  input  C_in,
  output S,
  output C_out
);

  wire and_1_out, and_2_out, xor_1_out;

  xor xor_1 (xor_1_out, A, B);
  xor xor_2 (S, xor_1_out, C_in);
  and and_1 (and_1_out, xor_1_out, C_in);
  and and_2 (and_2_out, A, B);
  or or_1 (C_out, and_1_out, and_2_out);
endmodule

module ImmGen (
  input  [31:0] Instrcutions,
  output [31:0] IMM32
);

  Multiplexer #(.enable("false"), .width(4)) multiplexer_1 (
    .in0(Instrcutions[24:21]), .in1(Instrcutions[11:8]), .out(IMM32[4:1]), .sel(Instrcutions[5]));
  Multiplexer #(.enable("false")) multiplexer_2 (
    .in0(Instrcutions[31]), .in1(Instrcutions[7]), .out(IMM32[11]), .sel(Instrcutions[6]));
  assign IMM32[31:12] = {{19{Instrcutions[31]}}, Instrcutions[31]};  // Bit_Extender bit_extender_1
  Multiplexer #(.enable("false"), .select(2)) multiplexer_3 (
    .in0(Instrcutions[20]), .in1(Instrcutions[7]), .in3(1'b0), .out(IMM32[0]), .sel(Instrcutions[6:5]));  // open: in2

  assign IMM32[10:5] = Instrcutions[30:25];

  // Other names for the same wires on the sheet: I30_25[5:0] = Instrcutions[30:25]; I5 = Instrcutions[5];
  //   I6_5[1:0] = Instrcutions[6:5]; I6 = Instrcutions[6]; I7 = Instrcutions[7]; I11_8[3:0] = Instrcutions[11:8];
  //   I_20 = Instrcutions[20]; I24_21[3:0] = Instrcutions[24:21]; I31 = Instrcutions[31]
endmodule

module InstructionMemory (
  input  [23:0] Adress,
  input  Clock_in,
  output [31:0] instruction
);

  wire not_1_out;

  RAM #(.addrWidth(22), .asyncread("true"), .dataWidth(32)) ram_1 (
    .addr(Adress[23:2]), .we(1'b0), .oe(not_1_out), .dout(instruction));  // open: clk, din
  not not_1 (not_1_out, Clock_in);
endmodule

module DataMemory (
  input  [25:0] Address,
  input  MemWrite,
  input  MemRead,
  input  Clock_in,
  input  [31:0] WriteData,
  output [31:0] ReadData
);

  RAM #(.addrWidth(24), .asyncread("true"), .dataWidth(32)) ram_1 (
    .addr(Address[25:2]), .we(MemWrite), .oe(MemRead), .clk(Clock_in), .din(WriteData), .dout(ReadData));
endmodule

module RISCV (
);

  wire alu_control_1_alu_src, and_1_out, clock_1_out, comparator_1_eq, control_1_branch, control_1_memread,
       control_1_memtoreg, control_1_memwrite, control_1_regwrite;
  wire [3:0] alu_control_1_alu_ctrl0;
  wire [31:0] adder_1_out, adder_2_out, alu32_1_result, datamemory_1_readdata, immgen_1_imm32,
       instructionmemory_1_instruction, multiplexer_1_out, multiplexer_2_out, multiplexer_3_out,
       register_1_q, register_file_1_rdata1, register_file_1_rdata2;

  Register #(.width(32)) register_1 (
    .D(multiplexer_2_out), .en(1'b1), .clk(clock_1_out), .Q(register_1_q));  // open: clr
  Clock clock_1 (.out(clock_1_out));
  Adder #(.width(32)) adder_1 (.a(register_1_q), .b({32{1'b0}}), .out(adder_1_out));  // open: cin, cout
  InstructionMemory instructionmemory_1 (
    .Adress(register_1_q[23:0]), .Clock_in(clock_1_out), .instruction(instructionmemory_1_instruction));
  ALU_Control alu_control_1 (
    .i4(instructionmemory_1_instruction[4]), .i5(instructionmemory_1_instruction[5]),
    .i6(instructionmemory_1_instruction[6]), .i12(instructionmemory_1_instruction[12]),
    .i13(instructionmemory_1_instruction[13]), .i14(instructionmemory_1_instruction[14]),
    .i30(instructionmemory_1_instruction[30]), .ALU_Ctrl3(alu_control_1_alu_ctrl0[3]),
    .ALU_Ctrl2(alu_control_1_alu_ctrl0[2]), .ALU_Ctrl1(alu_control_1_alu_ctrl0[1]),
    .ALU_Ctrl0(alu_control_1_alu_ctrl0[0]), .ALU_SRC(alu_control_1_alu_src));
  register_file register_file_1 (
    .RReg1(instructionmemory_1_instruction[19:15]), .RReg2(instructionmemory_1_instruction[24:20]),
    .Clock_in(clock_1_out), .WData(multiplexer_3_out), .Write(control_1_regwrite),
    .WREG(instructionmemory_1_instruction[11:7]), .RData1(register_file_1_rdata1),
    .RData2(register_file_1_rdata2));
  ImmGen immgen_1 (.Instrcutions(instructionmemory_1_instruction), .IMM32(immgen_1_imm32));
  Control control_1 (
    .I6_0(instructionmemory_1_instruction[6:0]), .MemtoReg(control_1_memtoreg),
    .RegWrite(control_1_regwrite), .MemRead(control_1_memread), .MemWrite(control_1_memwrite),
    .Branch(control_1_branch));
  Multiplexer #(.enable("false"), .width(32)) multiplexer_1 (
    .in0(register_file_1_rdata2), .in1(immgen_1_imm32), .out(multiplexer_1_out), .sel(alu_control_1_alu_src));
  Comparator #(.width(32)) comparator_1 (
    .a(register_file_1_rdata1), .b(register_file_1_rdata2), .eq(comparator_1_eq));  // open: gt, lt
  Adder #(.width(32)) adder_2 (.a(register_1_q), .b(immgen_1_imm32), .out(adder_2_out));  // open: cin, cout
  and and_1 (and_1_out, control_1_branch, comparator_1_eq);
  ALU32 alu32_1 (
    .ALU_Ctrl(alu_control_1_alu_ctrl0), .A(register_file_1_rdata1), .B(multiplexer_1_out),
    .Result(alu32_1_result));  // open: C_out
  Multiplexer #(.enable("false"), .width(32)) multiplexer_2 (
    .in0(adder_1_out), .in1(adder_2_out), .out(multiplexer_2_out), .sel(and_1_out));
  DataMemory datamemory_1 (
    .Address(alu32_1_result[25:0]), .MemWrite(control_1_memwrite), .MemRead(control_1_memread),
    .Clock_in(clock_1_out), .WriteData(register_file_1_rdata2), .ReadData(datamemory_1_readdata));
  Multiplexer #(.enable("false"), .width(32)) multiplexer_3 (
    .in0(alu32_1_result), .in1(datamemory_1_readdata), .out(multiplexer_3_out), .sel(control_1_memtoreg));
endmodule

module Control (
  input  [6:0] I6_0,
  output MemtoReg,
  output RegWrite,
  output MemRead,
  output MemWrite,
  output Branch
);

  wire not_1_out, not_2_out;

  not not_1 (not_1_out, I6_0[6]);
  not not_2 (not_2_out, I6_0[5]);
  not not_3 (MemtoReg, I6_0[4]);
  or or_1 (RegWrite, not_2_out, I6_0[4]);
  and and_1 (MemRead, not_2_out, MemtoReg);
  and and_2 (MemWrite, not_1_out, I6_0[5], MemtoReg);

  assign Branch = I6_0[6];
endmodule

module register_file (
  input  [4:0] RReg1,
  input  [4:0] RReg2,
  input  Clock_in,
  input  [31:0] WData,
  input  Write,
  input  [4:0] WREG,
  output [31:0] RData1,
  output [31:0] RData2
);

  wire W3_0, W7_4, W11_8, W15_12, W19_16, W23_20, W27_24, W31_28;
  wire [31:0] register_file_4_32_1_rdata1, register_file_4_32_1_rdata2, test_1_rdata1, test_1_rdata2,
       test_2_rdata1, test_2_rdata2, test_3_rdata1, test_3_rdata2, test_4_rdata1, test_4_rdata2,
       test_5_rdata1, test_5_rdata2, test_6_rdata1, test_6_rdata2, test_7_rdata1, test_7_rdata2;

  Demultiplexer #(.enable("false"), .select(3)) demultiplexer_1 (
    .out0(W3_0), .out1(W7_4), .out2(W11_8), .out3(W15_12), .out4(W19_16), .out5(W23_20), .out6(W27_24),
    .out7(W31_28), .in(Write), .sel(WREG[4:2]));
  register_file_4_32 register_file_4_32_1 (
    .RReg1(RReg1[1:0]), .RReg2(RReg2[1:0]), .WData(WData), .Clock_In(Clock_in), .Write(W3_0),
    .WReg(WREG[1:0]), .RData1(register_file_4_32_1_rdata1), .RData2(register_file_4_32_1_rdata2));
  Test test_1 (
    .RReg1(RReg1[1:0]), .RReg2(RReg2[1:0]), .WData(WData), .Clock_In(Clock_in), .Write(W7_4),
    .WReg(WREG[1:0]), .RData1(test_1_rdata1), .RData2(test_1_rdata2));
  Test test_2 (
    .RReg1(RReg1[1:0]), .RReg2(RReg2[1:0]), .WData(WData), .Clock_In(Clock_in), .Write(W11_8),
    .WReg(WREG[1:0]), .RData1(test_2_rdata1), .RData2(test_2_rdata2));
  Test test_3 (
    .RReg1(RReg1[1:0]), .RReg2(RReg2[1:0]), .WData(WData), .Clock_In(Clock_in), .Write(W15_12),
    .WReg(WREG[1:0]), .RData1(test_3_rdata1), .RData2(test_3_rdata2));
  Test test_4 (
    .RReg1(RReg1[1:0]), .RReg2(RReg2[1:0]), .WData(WData), .Clock_In(Clock_in), .Write(W19_16),
    .WReg(WREG[1:0]), .RData1(test_4_rdata1), .RData2(test_4_rdata2));
  Test test_5 (
    .RReg1(RReg1[1:0]), .RReg2(RReg2[1:0]), .WData(WData), .Clock_In(Clock_in), .Write(W23_20),
    .WReg(WREG[1:0]), .RData1(test_5_rdata1), .RData2(test_5_rdata2));
  Test test_6 (
    .RReg1(RReg1[1:0]), .RReg2(RReg2[1:0]), .WData(WData), .Clock_In(Clock_in), .Write(W27_24),
    .WReg(WREG[1:0]), .RData1(test_6_rdata1), .RData2(test_6_rdata2));
  Test test_7 (
    .RReg1(RReg1[1:0]), .RReg2(RReg2[1:0]), .WData(WData), .Clock_In(Clock_in), .Write(W31_28),
    .WReg(WREG[1:0]), .RData1(test_7_rdata1), .RData2(test_7_rdata2));
  Multiplexer #(.enable("false"), .select(3), .width(32)) multiplexer_1 (
    .in0(register_file_4_32_1_rdata1), .in1(test_1_rdata1), .in2(test_2_rdata1), .in3(test_3_rdata1),
    .in4(test_4_rdata1), .in5(test_5_rdata1), .in6(test_6_rdata1), .in7(test_7_rdata1), .out(RData1),
    .sel(RReg1[4:2]));
  Multiplexer #(.enable("false"), .select(3), .width(32)) multiplexer_2 (
    .in0(register_file_4_32_1_rdata2), .in1(test_1_rdata2), .in2(test_2_rdata2), .in3(test_3_rdata2),
    .in4(test_4_rdata2), .in5(test_5_rdata2), .in6(test_6_rdata2), .in7(test_7_rdata2), .out(RData2),
    .sel(RReg2[4:2]));
endmodule

module ALU_Control (
  input  i4,
  input  i5,
  input  i6,
  input  i12,
  input  i13,
  input  i14,
  input  i30,
  output ALU_Ctrl3,
  output ALU_Ctrl2,
  output ALU_Ctrl1,
  output ALU_Ctrl0,
  output ALU_SRC
);

  wire xnor_1_out, xor_1_out;

  xnor xnor_1 (xnor_1_out, i13, i12);
  xor xor_1 (xor_1_out, i14, i6);
  nand nand_1 (ALU_Ctrl1, i14, i13);
  nand nand_2 (ALU_Ctrl0, xnor_1_out, xor_1_out);
  and and_1 (ALU_Ctrl2, i30, i5, i4);
  nand nand_3 (ALU_SRC, i5, i4);

  assign ALU_Ctrl3 = i6;
endmodule

module ALU32 (
  input  [3:0] ALU_Ctrl,
  input  [31:0] A,
  input  [31:0] B,
  output [31:0] Result,
  output C_out
);

  wire alu4_1_c_out, alu4_2_c_out, alu4_3_c_out, alu4_4_c_out, alu4_5_c_out, alu4_6_c_out, alu4_7_c_out;

  ALU4 alu4_1 (.ALU_Ctrl(ALU_Ctrl), .A(A[3:0]), .B(B[3:0]), .C_in(ALU_Ctrl[2]), .R(Result[3:0]), .C_out(alu4_1_c_out));
  ALU4 alu4_2 (
    .ALU_Ctrl(ALU_Ctrl), .A(A[15:12]), .B(B[15:12]), .C_in(alu4_4_c_out), .R(Result[15:12]),
    .C_out(alu4_2_c_out));
  ALU4 alu4_3 (.ALU_Ctrl(ALU_Ctrl), .A(A[7:4]), .B(B[7:4]), .C_in(alu4_1_c_out), .R(Result[7:4]), .C_out(alu4_3_c_out));
  ALU4 alu4_4 (
    .ALU_Ctrl(ALU_Ctrl), .A(A[11:8]), .B(B[11:8]), .C_in(alu4_3_c_out), .R(Result[11:8]), .C_out(alu4_4_c_out));
  ALU4 alu4_5 (
    .ALU_Ctrl(ALU_Ctrl), .A(A[19:16]), .B(B[19:16]), .C_in(alu4_2_c_out), .R(Result[19:16]),
    .C_out(alu4_5_c_out));
  ALU4 alu4_6 (
    .ALU_Ctrl(ALU_Ctrl), .A(A[23:20]), .B(B[23:20]), .C_in(alu4_5_c_out), .R(Result[23:20]),
    .C_out(alu4_6_c_out));
  ALU4 alu4_7 (
    .ALU_Ctrl(ALU_Ctrl), .A(A[27:24]), .B(B[27:24]), .C_in(alu4_6_c_out), .R(Result[27:24]),
    .C_out(alu4_7_c_out));
  ALU4 alu4_8 (.ALU_Ctrl(ALU_Ctrl), .A(A[31:28]), .B(B[31:28]), .C_in(alu4_7_c_out), .R(Result[31:28]), .C_out(C_out));
endmodule

module ALU4 (
  input  [3:0] ALU_Ctrl,
  input  [3:0] A,
  input  [3:0] B,
  input  C_in,
  output [3:0] R,
  output C_out
);

  wire one_bit_1_c_out, one_bit_2_c_out, one_bit_3_c_out;

  one_bit one_bit_1 (.ALU_Ctrl(ALU_Ctrl), .A(A[0]), .B(B[0]), .C_in(C_in), .R(R[0]), .C_out(one_bit_1_c_out));
  one_bit one_bit_2 (
    .ALU_Ctrl(ALU_Ctrl), .A(A[1]), .B(B[1]), .C_in(one_bit_1_c_out), .R(R[1]), .C_out(one_bit_2_c_out));
  one_bit one_bit_3 (
    .ALU_Ctrl(ALU_Ctrl), .A(A[2]), .B(B[2]), .C_in(one_bit_2_c_out), .R(R[2]), .C_out(one_bit_3_c_out));
  one_bit one_bit_4 (.ALU_Ctrl(ALU_Ctrl), .A(A[3]), .B(B[3]), .C_in(one_bit_3_c_out), .R(R[3]), .C_out(C_out));
endmodule

module one_bit (
  input  [3:0] ALU_Ctrl,
  input  A,
  input  B,
  input  C_in,
  output R,
  output C_out
);

  wire and_1_out, main_1_s, multiplexer_1_out, not_1_out, or_1_out, xor_1_out;

  Multiplexer #(.enable("false")) multiplexer_1 (.in0(B), .in1(not_1_out), .out(multiplexer_1_out), .sel(ALU_Ctrl[2]));
  not not_1 (not_1_out, B);
  and and_1 (and_1_out, A, multiplexer_1_out);
  or or_1 (or_1_out, A, multiplexer_1_out);
  xor xor_1 (xor_1_out, A, multiplexer_1_out);
  main main_1 (.A(A), .B(multiplexer_1_out), .C_in(C_in), .S(main_1_s), .C_out(C_out));
  Multiplexer #(.enable("false"), .select(2)) multiplexer_2 (
    .in0(and_1_out), .in1(or_1_out), .in2(xor_1_out), .in3(main_1_s), .out(R), .sel(ALU_Ctrl[1:0]));
endmodule

module Test (
  input  [1:0] RReg1,
  input  [1:0] RReg2,
  input  [31:0] WData,
  input  Clock_In,
  input  Write,
  input  [1:0] WReg,
  output [31:0] RData1,
  output [31:0] RData2
);

  wire demultiplexer_1_out0, demultiplexer_1_out1, demultiplexer_1_out2, demultiplexer_1_out3;
  wire [31:0] register_1_q, register_2_q, register_3_q, register_4_q;

  Demultiplexer #(.enable("false"), .select(2)) demultiplexer_1 (
    .out0(demultiplexer_1_out0), .out1(demultiplexer_1_out1), .out2(demultiplexer_1_out2),
    .out3(demultiplexer_1_out3), .in(Write), .sel(WReg));
  Register #(.width(32)) register_1 (
    .D(WData), .en(demultiplexer_1_out0), .clk(Clock_In), .Q(register_1_q));  // open: clr
  Register #(.width(32)) register_2 (
    .D(WData), .en(demultiplexer_1_out1), .clk(Clock_In), .Q(register_2_q));  // open: clr
  Register #(.width(32)) register_3 (
    .D(WData), .en(demultiplexer_1_out2), .clk(Clock_In), .Q(register_3_q));  // open: clr
  Register #(.width(32)) register_4 (
    .D(WData), .en(demultiplexer_1_out3), .clk(Clock_In), .Q(register_4_q));  // open: clr
  Multiplexer #(.enable("false"), .select(2), .width(32)) multiplexer_1 (
    .in0(register_1_q), .in1(register_2_q), .in2(register_3_q), .in3(register_4_q), .out(RData1), .sel(RReg1));
  Multiplexer #(.enable("false"), .select(2), .width(32)) multiplexer_2 (
    .in0(register_1_q), .in1(register_2_q), .in2(register_3_q), .in3(register_4_q), .out(RData2), .sel(RReg2));
endmodule

module register_file_4_32 (
  input  [1:0] RReg1,
  input  [1:0] RReg2,
  input  [31:0] WData,
  input  Clock_In,
  input  Write,
  input  [1:0] WReg,
  output [31:0] RData1,
  output [31:0] RData2
);

  wire demultiplexer_1_out0, demultiplexer_1_out1, demultiplexer_1_out2, demultiplexer_1_out3;
  wire [31:0] register_1_q, register_2_q, register_3_q, register_4_q;

  Demultiplexer #(.enable("false"), .select(2)) demultiplexer_1 (
    .out0(demultiplexer_1_out0), .out1(demultiplexer_1_out1), .out2(demultiplexer_1_out2),
    .out3(demultiplexer_1_out3), .in(Write), .sel(WReg));
  Register #(.width(32)) register_1 (
    .D(WData), .en(demultiplexer_1_out0), .clk(Clock_In), .Q(register_1_q), .clr(Write));
  Register #(.width(32)) register_2 (
    .D(WData), .en(demultiplexer_1_out1), .clk(Clock_In), .Q(register_2_q));  // open: clr
  Register #(.width(32)) register_3 (
    .D(WData), .en(demultiplexer_1_out2), .clk(Clock_In), .Q(register_3_q));  // open: clr
  Register #(.width(32)) register_4 (
    .D(WData), .en(demultiplexer_1_out3), .clk(Clock_In), .Q(register_4_q));  // open: clr
  Multiplexer #(.enable("false"), .select(2), .width(32)) multiplexer_1 (
    .in0(register_1_q), .in1(register_2_q), .in2(register_3_q), .in3(register_4_q), .out(RData1), .sel(RReg1));
  Multiplexer #(.enable("false"), .select(2), .width(32)) multiplexer_2 (
    .in0(register_1_q), .in1(register_2_q), .in2(register_3_q), .in3(register_4_q), .out(RData2), .sel(RReg2));
endmodule
